# Fritzing sketch Llunatics_CanSat (saved by Fritzing 0.9.3b)

parts:
  Componente2 = Arduino Nano (Rev3.0)
  SD_card_module1 = SD Card Module
  GY-NEO6MV3 = SUP500F [package=sup500f]
  Componente4 = APC220 with antenna
  BMP280_Breakout2 = BMP280 Breakout Board [part_number=BMP280]
  GY1 = GY-521 (MPU-6050) [form="♀ (female)" package=THT]
  buz1 = Piezo Buzzer
  R2 = Photocell (LDR) [package=THT]
  R3 = Resistor [tolerance=±5% resistance=10k package=THT]
  元件1 = Current Sensor 5A
  R4 = Resistor [tolerance=±5% resistance=220 package=THT]
  VCC1 = Battery block 9V

nets:
  N1: Componente2.D1/TX, GY-NEO6MV3.GND
  N2: Componente2.D0/RX, GY-NEO6MV3.VCC
  N3: Componente2.D6, Componente4.RXD
  N4: Componente2.D7, Componente4.TXD
  N5: Componente2.D8, buz1.pin_2
  N6: Componente2.D9, SD_card_module1.CS
  N7: Componente2.D11/MOSI, SD_card_module1.MOSI
  N8: Componente2.D12/MISO, SD_card_module1.MISO
  N9: Componente2.VIN, VCC1.+
  GND: Componente2.GND, SD_card_module1.GND, GY-NEO6MV3.RX-I, Componente4.GND, BMP280_Breakout2.GND, GY1.pin2, R3.Pin_1, 元件1.GND, R4.Pin_0, VCC1.-
  VCC: Componente2.5V, SD_card_module1.+5, GY-NEO6MV3.TX-O, Componente4.VCC, GY1.pin1, R2.pin_1, 元件1.VCC
  N10: Componente2.A5, BMP280_Breakout2.SCL, GY1.pin3
  N11: Componente2.A4, BMP280_Breakout2.SDA, GY1.pin4
  N12: Componente2.A1, 元件1.2, 元件1.OUT
  N13: Componente2.A0, R2.pin_0, R3.Pin_0
  3V3: Componente2.3V3, BMP280_Breakout2.VCC
  N14: Componente2.D13/SCK, SD_card_module1.SCK
  N15: buz1.pin_1, R4.Pin_1

notes:
  GND: Black
  VCC: Red
  RX: Yellow
  TX: Green
  APC 220
  Lector MicroSD
  Buzzer
  BMP280
  MPU-9250
  LDR sensor
  ACS 712
  RECTENNA

custom parts:
  SD Card Module: SD Card Module Slot Socket Reader For Arduino ARM MCU
  APC220 with antenna: Radio transceiver module for Arduino operating in the 418-455MHz band.
  BMP280 Breakout Board: This is a breakout board for the Bosch Sensortec BMP280, "an absolute barometric pressure sensor especially designed for mobile applications." The operation range is 300 to 1100 hPa. Supply voltage is 1.2 to 3.6V. Operating temperature range is -40 to +85 °C.
  GY-521 (MPU-6050): Placa GY-521 basada en conjunto de acelerómetro+giroscopios MPU-6050
  Piezo Buzzer: Part from https://www.nutsvolts.com/magazine/article/november2012_SmileysWorkshop modified to be .3 in spacing to match the adafruit buzzer 5V breadboard friendly part.
